# Fritzing sketch schema (saved by Fritzing 0.8.5b)
breadboards: 1

parts:
  U1 = attiny85 [package=dip]
  BAT1 = Battery Holders [package=battcom_20mm_pth]
  S1 = Momentary Switch [package=ksa_sealed_tac_switch]
  LED1 = LED - 3mm [color="Red (633nm)" package="3 mm [THT]"]
  R1 = Resistor [tolerance=±5% resistance=220 package=THT]
  Q1 = NPN-Transistor [part_number=BC547 package="TO92 [THT]"]
  R2 = Resistor [tolerance=±5% resistance=1k package=THT]
  J1 = Piezo Speaker

nets:
  N1: U1.Pin_1, S1.2
  GND: U1.Pin_4, BAT1.-, S1.4, LED1.cathode, J1.pin2
  N2: U1.Pin_5, R2.Pin_1
  N3: U1.Pin_7, R1.Pin_0
  N4: U1.Pin_8, BAT1.+, Q1.C
  N5: LED1.anode, R1.Pin_1
  N6: Q1.E, J1.pin1
  N7: Q1.B, R2.Pin_0
